# Fritzing sketch quadcopter (saved by Fritzing 0.9.3b)
circuit board: 8.46667cm x 5.64444cm

parts:
  Componente3 = Arduino Nano (Rev3.0)
  10DOF2 = CJMCU-10DOF [form="♀ (female)" package=THT]
  Componente4 = Barometric Pressure Sensor - BMP180 Breakout (GY-68)
  DJI_ESC_30A1 = DJI 30A ESC
  DJI_ESC_30A2 = DJI 30A ESC
  DJI_ESC_30A3 = DJI 30A ESC
  DJI_ESC_30A4 = DJI 30A ESC
  Componente5 = NRF24L01+ Breakout Board
  hc-sr1 = hc-sr04

nets:
  GND: Componente3.GND, 10DOF2.GND, Componente4.GND, DJI_ESC_30A1.GND, DJI_ESC_30A2.GND, DJI_ESC_30A3.GND, DJI_ESC_30A4.GND, Componente5.GND, hc-sr1.GND
  N1: Componente3.D2, hc-sr1.Trig
  N2: Componente3.D3, DJI_ESC_30A4.DATA
  N3: Componente3.D4, hc-sr1.Echo
  N4: Componente3.D5, DJI_ESC_30A3.DATA
  N5: Componente3.D6, DJI_ESC_30A2.DATA_OUT
  N6: Componente3.D8, Componente5.CE
  N7: Componente3.D9, DJI_ESC_30A1.DATA, DJI_ESC_30A1.PWR_OUT
  N8: Componente3.D10, Componente5.CS
  N9: Componente3.D11/MOSI, Componente5.MOSI
  N10: Componente3.D12/MISO, Componente5.MISO
  5V: Componente3.5V, 10DOF2.+3V3, hc-sr1.VCC
  N11: Componente3.A5, 10DOF2.SCL, Componente4.SCL
  N12: Componente3.A4, 10DOF2.SDA, Componente4.SDA
  VCC: Componente3.3V3, Componente4.VCC, Componente5.VCC
  N13: Componente3.D13/SCK, Componente5.SCK

custom parts:
  CJMCU-10DOF: Placa CJMCU 10DOF basada en conjunto de acelerómetro+giroscopios+magnetómetro MPU-9250 y un barómetro BMP180
